// Logisim project project3.circ as structural Verilog: 2 circuits, main circuit main
// T0
module main (
  input  in_1,
  output [15:0] out_2
);

  wire clock_1_out, D0_LD, D1_ST, D2_MOV, D3_PSH, D4_PUL, D5_ADD, D6_SUB, D7_DEC, D8_INC, D9_AND, D10_OR,
       D11_NOT, D12_LSL, D13_LSR, D14_BRA, D15_BEQ, D16_BNE, D17_CALL, D18_RET, IR_EN, IR_LH, MEM_LD,
       MEM_SEL, MEM_STR, MuxCSel, T0, T1, T2, T3, T4, T5, T6, T7;
  wire [1:0] _3RB_FS, _4RB_FS, IR_FS, MuxASel, MuxBSel, OutCSel, OutDSel;
  wire [3:0] _3RB_RS, _4RB_RS;
  wire [15:11] INSTR;

  counter counter_1 (
    .out_2(T0), .out_3(T1), .out_4(T2), .out_5(T3), .out_6(T4), .out_7(T5), .out_8(T6), .out_9(T7),
    .in_1(in_1));
  assign OutCSel = T0 ? 2'b00 : 2'bz;  // Controlled_Buffer controlled_buffer_1
  assign OutDSel = T0 ? 2'b01 : 2'bz;  // Controlled_Buffer controlled_buffer_2
  assign _3RB_FS = T0 ? 2'b01 : 2'bz;  // Controlled_Buffer controlled_buffer_3
  assign _3RB_RS = T0 ? 4'b0011 : 4'bz;  // Controlled_Buffer controlled_buffer_4
  assign MuxASel = T0 ? 2'b01 : 2'bz;  // Controlled_Buffer controlled_buffer_5
  assign MuxBSel = T0 ? 2'b11 : 2'bz;  // Controlled_Buffer controlled_buffer_6
  assign MuxCSel = T0 ? 1'b0 : 1'bz;  // Controlled_Buffer controlled_buffer_7
  assign MEM_SEL = T0 ? 1'b1 : 1'bz;  // Controlled_Buffer controlled_buffer_8
  assign MEM_LD = T0 ? 1'b1 : 1'bz;  // Controlled_Buffer controlled_buffer_9
  assign MEM_STR = T0 ? 1'b0 : 1'bz;  // Controlled_Buffer controlled_buffer_10
  Decoder #(.select(5)) decoder_1 (
    .out0(D0_LD), .out1(D1_ST), .out2(D2_MOV), .out3(D3_PSH), .out4(D4_PUL), .out5(D5_ADD), .out6(D6_SUB),
    .out7(D7_DEC), .out8(D8_INC), .out9(D9_AND), .out10(D10_OR), .out11(D11_NOT), .out12(D12_LSL),
    .out13(D13_LSR), .out14(D14_BRA), .out15(D15_BEQ), .out16(D16_BNE), .out17(D17_CALL), .out18(D18_RET),
    .sel(INSTR), .en(T3));  // open: out19, out20, out21, out22, out23, out24, out25, out26, out27, out28, out29, out30, out31
  assign MEM_SEL = T1 ? 1'b1 : 1'bz;  // Controlled_Buffer controlled_buffer_11
  assign MEM_LD = T1 ? 1'b1 : 1'bz;  // Controlled_Buffer controlled_buffer_12
  assign _3RB_FS = T1 ? 2'b10 : 2'bz;  // Controlled_Buffer controlled_buffer_13
  assign _3RB_RS = T1 ? 4'b0001 : 4'bz;  // Controlled_Buffer controlled_buffer_14
  assign IR_EN = T1 ? 1'b1 : 1'bz;  // Controlled_Buffer controlled_buffer_15
  assign IR_FS = T1 ? 2'b11 : 2'bz;  // Controlled_Buffer controlled_buffer_16
  assign IR_LH = T1 ? 1'b0 : 1'bz;  // Controlled_Buffer controlled_buffer_17
  assign MuxCSel = T1 ? 1'b0 : 1'bz;  // Controlled_Buffer controlled_buffer_18
  assign MuxASel = T1 ? 2'b10 : 2'bz;  // Controlled_Buffer controlled_buffer_19
  assign MEM_STR = T1 ? 1'b0 : 1'bz;  // Controlled_Buffer controlled_buffer_20
  assign IR_LH = T2 ? 1'b1 : 1'bz;  // Controlled_Buffer controlled_buffer_21
  assign _3RB_RS = T2 ? 4'b0001 : 4'bz;  // Controlled_Buffer controlled_buffer_22
  assign OutDSel = T2 ? 2'b00 : 2'bz;  // Controlled_Buffer controlled_buffer_23
  assign MEM_SEL = T2 ? 1'b1 : 1'bz;  // Controlled_Buffer controlled_buffer_24
  assign MEM_LD = T2 ? 1'b1 : 1'bz;  // Controlled_Buffer controlled_buffer_25
  assign IR_EN = T2 ? 1'b1 : 1'bz;  // Controlled_Buffer controlled_buffer_26
  assign IR_FS = T2 ? 2'b11 : 2'bz;  // Controlled_Buffer controlled_buffer_27
  assign _3RB_FS = T2 ? 2'b10 : 2'bz;  // Controlled_Buffer controlled_buffer_28
  assign MEM_STR = T2 ? 1'b0 : 1'bz;  // Controlled_Buffer controlled_buffer_29
  assign IR_EN = T3 ? 1'b0 : 1'bz;  // Controlled_Buffer controlled_buffer_30
  assign OutDSel = T3 ? 2'b00 : 2'bz;  // Controlled_Buffer controlled_buffer_31
  assign MEM_SEL = T3 ? 1'b1 : 1'bz;  // Controlled_Buffer controlled_buffer_32
  assign MEM_LD = T3 ? 1'b1 : 1'bz;  // Controlled_Buffer controlled_buffer_33
  assign MEM_STR = T3 ? 1'b0 : 1'bz;  // Controlled_Buffer controlled_buffer_34
  Clock clock_1 (.out(clock_1_out));
  part2_main main_1 (
    .FunSel_2(_4RB_FS), .RegSel(_4RB_RS), .MuxASel(MuxASel), .OutCSel(OutCSel), .OutDSel(OutDSel),
    .FunSel_3(_3RB_FS), .RegSel_2(_3RB_RS), .L_H(IR_LH), .Enable(IR_EN), .FunSel_4(IR_FS), .MuxCSel(MuxCSel),
    .MuxBSel(MuxBSel), .FunSel(4'b0000), .in_10(MEM_STR), .in_11(MEM_SEL), .in_12(MEM_LD), .out_23(out_2),
    .in_2(clock_1_out));  // open: OutASel, OutBSel, out_21, in_13, out_22
  Hex_Digit_Display hex_digit_display_1 (.value(out_2[15:12]));  // open: dp
  Hex_Digit_Display hex_digit_display_2 (.value(out_2[7:4]));  // open: dp
  Hex_Digit_Display hex_digit_display_3 (.value(out_2[11:8]));  // open: dp
  Hex_Digit_Display hex_digit_display_4 (.value(out_2[3:0]));  // open: dp

  // Other names for the same wires on the sheet: OPCODE[4:0] = INSTR; SCR = in_1
endmodule

module counter (
  input  in_1,
  output out_2,
  output out_3,
  output out_4,
  output out_5,
  output out_6,
  output out_7,
  output out_8,
  output out_9
);

  wire clock_1_out;
  wire [2:0] counter_1_q;

  Counter #(.width(3), .max('h7)) counter_1 (
    .Q(counter_1_q), .clk(clock_1_out), .clr(in_1));  // open: load, D, count, carry
  Clock clock_1 (.out(clock_1_out));
  Decoder #(.select(3), .enable("false")) decoder_1 (
    .out0(out_2), .out1(out_3), .out2(out_4), .out3(out_5), .out4(out_6), .out5(out_7), .out6(out_8),
    .out7(out_9), .sel(counter_1_q));
endmodule
